// Logisim project bench.circ as structural Verilog: 2 circuits, main circuit main
module main (
  input  [3:0] b,
  input  sub_notadd,
  input  [3:0] a,
  output [3:0] s,
  output cout
);

  wire fa1_s1, fa2_s1, fa3_s1, xor_1_out, xor_2_out, xor_3_out, xor_4_out;

  xor xor_1 (xor_1_out, b[0], sub_notadd);
  xor xor_2 (xor_2_out, b[1], sub_notadd);
  xor xor_3 (xor_3_out, b[2], sub_notadd);
  xor xor_4 (xor_4_out, b[3], sub_notadd);
  fulladder fa1 (.a(sub_notadd), .b(xor_1_out), .c(a[0]), .s0(s[0]), .s1(fa1_s1));
  fulladder fa2 (.a(fa1_s1), .b(xor_2_out), .c(a[1]), .s0(s[1]), .s1(fa2_s1));
  fulladder fa3 (.a(fa2_s1), .b(xor_3_out), .c(a[2]), .s0(s[2]), .s1(fa3_s1));
  fulladder fa4 (.a(fa3_s1), .b(xor_4_out), .c(a[3]), .s0(s[3]), .s1(cout));
endmodule

module fulladder (
  input  a,
  input  b,
  input  c,
  output s0,
  output s1
);

  wire and_1_out, and_2_out, and_3_out, xor_1_out;

  and and_1 (and_1_out, a, b);
  and and_2 (and_2_out, a, c);
  or or_1 (s1, and_1_out, and_2_out, and_3_out);
  and and_3 (and_3_out, b, c);
  xor xor_1 (xor_1_out, a, b);
  xor xor_2 (s0, xor_1_out, c);
endmodule
